// Logisim project real_alu.circ as structural Verilog: 13 circuits, main circuit main
module main (
);


  // Notes on the sheet:
  //   REAL_ALU
endmodule

module Logic_Unit (
  input  [7:0] inA,
  input  Sel2,
  input  Sel1,
  input  Sel0,
  input  [7:0] inB,
  output [7:0] aluOut,
  output OF
);

  wire dxshiftinb_1_of, logicdecoder_1_out_4, logicdecoder_1_out_5, logicdecoder_1_out_6,
       logicdecoder_1_out_7, logicdecoder_1_out_8, sxshiftinb_1_of;
  wire [7:0] dxshiftinb_1_aluout, ina_inb_1_aluout, inaorinb_1_aluout, notinb_1_aluout, sxshiftinb_1_aluout;

  inA_inB ina_inb_1 (.inA(inA), .in_2(logicdecoder_1_out_4), .inB(inB), .aluOut(ina_inb_1_aluout));
  inAorinB inaorinb_1 (.in_3(logicdecoder_1_out_5), .inA(inA), .inB(inB), .aluOut(inaorinb_1_aluout));
  LogicDecoder logicdecoder_1 (
    .out_4(logicdecoder_1_out_4), .out_5(logicdecoder_1_out_5), .out_6(logicdecoder_1_out_6),
    .out_7(logicdecoder_1_out_7), .out_8(logicdecoder_1_out_8), .Sel2(Sel2), .Sel1(Sel1), .Sel0(Sel0));
  NotinB notinb_1 (.in_2(logicdecoder_1_out_6), .inB(inB), .aluout(notinb_1_aluout));
  assign aluOut = ina_inb_1_aluout | inaorinb_1_aluout | notinb_1_aluout | sxshiftinb_1_aluout | dxshiftinb_1_aluout;  // OR_Gate or_1, 8 bits wide
  SxShiftinB sxshiftinb_1 (.inB(inB), .in_2(logicdecoder_1_out_7), .OF(sxshiftinb_1_of), .aluOut(sxshiftinb_1_aluout));
  DxshiftinB dxshiftinb_1 (.inB(inB), .OF(dxshiftinb_1_of), .aluOut(dxshiftinb_1_aluout), .in_2(logicdecoder_1_out_8));
  or or_2 (OF, sxshiftinb_1_of, dxshiftinb_1_of);
endmodule

module inA_inB (
  input  [7:0] inA,
  input  in_2,
  input  [7:0] inB,
  output [7:0] aluOut
);

  wire [7:0] bit_extender_1_out;

  assign bit_extender_1_out = {{7{in_2}}, in_2};  // Bit_Extender bit_extender_1
  assign aluOut = inA & bit_extender_1_out & inB;  // AND_Gate and_1, 8 bits wide
endmodule

module inAorinB (
  input  [7:0] inA,
  input  [7:0] inB,
  input  in_3,
  output [7:0] aluOut
);

  wire [7:0] bit_extender_1_out, or_1_out;

  assign bit_extender_1_out = {{7{in_3}}, in_3};  // Bit_Extender bit_extender_1
  assign or_1_out = inA | inB;  // OR_Gate or_1, 8 bits wide
  assign aluOut = bit_extender_1_out & or_1_out;  // AND_Gate and_1, 8 bits wide
endmodule

module NotinB (
  input  [7:0] inB,
  input  in_2,
  output [7:0] aluout
);

  wire [7:0] bit_extender_1_out, not_1_out;

  assign bit_extender_1_out = {{7{in_2}}, in_2};  // Bit_Extender bit_extender_1
  assign not_1_out = ~inB;  // NOT_Gate not_1, 8 bits wide
  assign aluout = bit_extender_1_out & not_1_out;  // AND_Gate and_1, 8 bits wide
endmodule

module SxShiftinB (
  input  [7:0] inB,
  input  in_2,
  output OF,
  output [7:0] aluOut
);

  wire [6:0] bit_extender_1_out;

  and and_1 (OF, in_2, inB[7]);
  assign aluOut[7:1] = inB[6:0] & bit_extender_1_out;  // AND_Gate and_2, 7 bits wide
  assign bit_extender_1_out = {{6{in_2}}, in_2};  // Bit_Extender bit_extender_1

  assign aluOut[0] = 1'b0;
endmodule

module DxshiftinB (
  input  [7:0] inB,
  input  in_2,
  output OF,
  output [7:0] aluOut
);

  wire [6:0] bit_extender_1_out;

  assign bit_extender_1_out = {{6{in_2}}, in_2};  // Bit_Extender bit_extender_1
  and and_1 (OF, in_2, inB[0]);
  assign aluOut[6:0] = inB[7:1] & bit_extender_1_out;  // AND_Gate and_2, 7 bits wide

  assign aluOut[7] = 1'b0;
endmodule

module LogicDecoder (
  input  Sel2,
  input  Sel1,
  input  Sel0,
  output out_4,
  output out_5,
  output out_6,
  output out_7,
  output out_8
);

  wire not_1_out, not_2_out, not_3_out;

  not not_1 (not_1_out, Sel2);
  not not_2 (not_2_out, Sel1);
  not not_3 (not_3_out, Sel0);
  and and_1 (out_4, not_1_out, not_2_out, not_3_out);
  and and_2 (out_5, not_1_out, not_2_out, Sel0);
  and and_3 (out_6, not_1_out, Sel1, not_3_out);
  and and_4 (out_7, not_1_out, Sel1, Sel0);
  and and_5 (out_8, Sel2, not_2_out, not_3_out);
endmodule

module halfadder (
  input  A,
  input  B,
  output S,
  output C
);

  xor xor_1 (S, A, B);
  and and_1 (C, B, A);
endmodule

module fulladder (
  input  A,
  input  B,
  input  Cin,
  output Cout,
  output S
);

  wire halfadder_1_c, halfadder_1_s, halfadder_2_c;

  halfadder halfadder_1 (.A(A), .B(B), .S(halfadder_1_s), .C(halfadder_1_c));
  halfadder halfadder_2 (.A(halfadder_1_s), .B(Cin), .S(S), .C(halfadder_2_c));
  or or_1 (Cout, halfadder_1_c, halfadder_2_c);
endmodule

module inA_add_inB_1 (
  input  in_1,
  input  in_2,
  input  in_3,
  input  in_4,
  input  in_5,
  input  in_6,
  input  in_7,
  input  in_8,
  input  in_9,
  input  in_10,
  input  in_11,
  input  in_12,
  input  in_13,
  input  in_14,
  input  in_15,
  input  in_16,
  input  in_17,
  input  in_18,
  output out_19,
  output out_20,
  output out_21,
  output out_22,
  output out_23,
  output out_24,
  output out_25,
  output out_26,
  output out_27
);

  wire fulladder_2_cout, fulladder_3_cout, fulladder_4_cout, fulladder_5_cout, fulladder_6_cout,
       fulladder_7_cout, fulladder_8_cout, fulladder_9_cout, fulladder_9_s, or_1_out;

  fulladder fulladder_1 (.A(in_2), .B(in_1), .Cin(fulladder_2_cout), .Cout(out_19), .S(out_20));
  fulladder fulladder_2 (.A(in_4), .B(in_3), .Cin(fulladder_3_cout), .Cout(fulladder_2_cout), .S(out_21));
  fulladder fulladder_3 (.A(in_6), .B(in_5), .Cin(fulladder_4_cout), .Cout(fulladder_3_cout), .S(out_22));
  fulladder fulladder_4 (.A(in_8), .B(in_7), .Cin(fulladder_5_cout), .Cout(fulladder_4_cout), .S(out_23));
  fulladder fulladder_5 (.A(in_10), .B(in_9), .Cin(fulladder_6_cout), .Cout(fulladder_5_cout), .S(out_24));
  fulladder fulladder_6 (.A(in_12), .B(in_11), .Cin(fulladder_7_cout), .Cout(fulladder_6_cout), .S(out_25));
  fulladder fulladder_7 (.A(in_14), .B(in_13), .Cin(fulladder_8_cout), .Cout(fulladder_7_cout), .S(out_26));
  fulladder fulladder_8 (.A(in_16), .B(in_15), .Cin(or_1_out), .Cout(fulladder_8_cout), .S(out_27));
  fulladder fulladder_9 (.A(in_18), .B(in_17), .Cin(1'b0), .Cout(fulladder_9_cout), .S(fulladder_9_s));
  or or_1 (or_1_out, fulladder_9_cout, fulladder_9_s);
endmodule

module inA_sub_inB (
  input  [7:0] B,
  input  [7:0] A
);

  inA_add_inB_1 ina_add_inb_1_1 (
    .in_1(B[7]), .in_2(A[7]), .in_3(B[6]), .in_4(A[6]), .in_5(B[5]), .in_6(A[5]), .in_7(B[4]), .in_8(A[4]),
    .in_9(B[3]), .in_10(A[3]), .in_11(B[2]), .in_12(A[2]), .in_13(B[1]), .in_14(A[1]), .in_15(B[0]),
    .in_16(A[0]));  // open: out_20, out_21, out_22, out_23, out_24, out_25, out_26, out_27, in_17, in_18, out_19
endmodule

module inA_add_inB (
);

  inA_add_inB_1 ina_add_inb_1_1 ();  // open: out_20, out_21, out_22, out_23, out_24, out_25, out_26, out_27, in_1, in_2, in_3, in_4, in_5, in_6, in_7, in_8, in_9, in_10, in_11, in_12, in_13, in_14, in_15, in_16, in_17, in_18, out_19
endmodule
